// Logisim project Lab1.circ as structural Verilog: 3 circuits, main circuit main
module main (
);


  // Notes on the sheet:
  //   Lab 1
  //   Dillon Gutowski
  //   Jacobo Belilty
endmodule

module part2 (
  input  A,
  input  A_S,
  input  B,
  input  B_S,
  input  V_S,
  input  V,
  input  W_S,
  input  W,
  input  X_S,
  input  X,
  input  Y_S,
  input  Y,
  output F_S,
  output F,
  output Z_S,
  output Z
);

  wire and_1_out, and_2_out, and_3_out, and_4_out, and_5_out, and_6_out, and_7_out, not_1_out, not_2_out,
       not_3_out, not_4_out, not_5_out, not_6_out, or_1_out, or_2_out;

  not not_1 (not_1_out, B);
  not not_2 (not_2_out, A);
  not not_3 (not_3_out, V);
  not not_4 (not_4_out, V);
  and and_1 (and_1_out, A, B);
  and and_2 (and_2_out, A, not_1_out);
  and and_3 (and_3_out, not_2_out, B);
  and and_4 (and_4_out, not_3_out, W);
  and and_5 (and_5_out, not_4_out, W);
  or or_1 (or_1_out, and_4_out, X);
  or or_2 (or_2_out, X, and_5_out);
  not not_5 (not_5_out, Y);
  or or_3 (F, and_1_out, and_2_out, and_3_out);
  and and_6 (and_6_out, or_2_out, not_5_out);
  or or_4 (Z, or_1_out, and_6_out);
  not not_6 (not_6_out, V_S);
  or or_5 (F_S, A_S, B_S);
  and and_7 (and_7_out, not_6_out, W_S);
  or or_6 (Z_S, and_7_out, X_S);

  // Notes on the sheet:
  //   Lab 1, Part 2
  //   A
  //   B
  //   A, simplified
  //   B, simplified
endmodule

module part3c (
  input  D,
  input  W,
  input  M,
  output A,
  output S
);

  wire and_1_out, not_1_out;

  and and_1 (and_1_out, D, W);
  not not_1 (not_1_out, and_1_out);
  and and_2 (A, not_1_out, M);
  or or_1 (S, M, not_1_out);

  // Notes on the sheet:
  //   Lab 1, part 3c
  //   Alarm
  //   Security Camera
endmodule
